# Fritzing sketch schematic (saved by Fritzing 0.9.0b)
circuit board: 6.202cm x 4.21479cm
breadboards: 1

parts:
  switch = Toggle Switch [package=THT]
  470 = Resistor [tolerance=±5% resistance=470 package=THT]
  cap = Electrolytic Capacitor [capacitance=100µF voltage=20V package="100 mil [THT, electrolytic]"]
  TRINKET1 = Trinket 5V
  10k = Resistor [tolerance=±5% resistance=10k package=THT]
  2 = screw terminal, 2 pins
  pressure_sensor = screw terminal, 2 pins
  power = screw terminal, 2 pins
  1 = screw terminal, 2 pins

nets:
  N1: switch.COM, cap.+, TRINKET1.no_name_yet#1, 2.pin1, pressure_sensor.pin2
  N2: switch.L2, power.pin2
  N3: 470.Pin_0, power.pin1
  N4: 470.Pin_1, TRINKET1.no_name_yet#4, pressure_sensor.pin1
  N5: cap.-, TRINKET1.no_name_yet#2, 2.pin2
  N6: TRINKET1.no_name_yet#7, 10k.Pin_0
  N7: 10k.Pin_1, 1.pin2

custom parts:
  Trinket 5V: Adafruit Trinket 5V
